// Logisim project trabalho.circ as structural Verilog: 5 circuits, main circuit main
module main (
  input  b4,
  input  b3,
  input  b2,
  input  b1,
  input  b0,
  input  a4,
  input  a3,
  input  a2,
  input  a1,
  input  a0
);

  wire multiplicador_1_s0, multiplicador_1_s1, multiplicador_1_s2, multiplicador_1_s3, multiplicador_1_s4,
       multiplicador_1_s5, multiplicador_1_s6, multiplicador_1_s7, multiplicador_1_s8, multiplicador_1_s9;

  LED s9 (.in(multiplicador_1_s9));
  LED s8 (.in(multiplicador_1_s8));
  LED s7 (.in(multiplicador_1_s7));
  LED s6 (.in(multiplicador_1_s6));
  LED s5 (.in(multiplicador_1_s5));
  LED s4 (.in(multiplicador_1_s4));
  multiplicador multiplicador_1 (
    .s1(multiplicador_1_s1), .s6(multiplicador_1_s6), .s2(multiplicador_1_s2), .s3(multiplicador_1_s3),
    .s5(multiplicador_1_s5), .s4(multiplicador_1_s4), .s8(multiplicador_1_s8), .s9(multiplicador_1_s9),
    .s0(multiplicador_1_s0), .s7(multiplicador_1_s7), .a0(a0), .a1(a1), .a2(a2), .a3(a3), .a4(a4), .b0(b0),
    .b1(b1), .b2(b2), .b3(b3), .b4(b4));
  LED s3 (.in(multiplicador_1_s3));
  LED s2 (.in(multiplicador_1_s2));
  LED s1 (.in(multiplicador_1_s1));
  LED s0 (.in(multiplicador_1_s0));
endmodule

module multiplicador (
  input  a0,
  input  a1,
  input  a2,
  input  a3,
  input  a4,
  input  b0,
  input  b1,
  input  b2,
  input  b3,
  input  b4,
  output s0,
  output s1,
  output s2,
  output s3,
  output s4,
  output s5,
  output s6,
  output s7,
  output s8,
  output s9
);

  wire addernor_2_out_4, addernor_2_out_5, addernor_3_out_4, addernor_3_out_5, addernor_4_out_4,
       addernor_4_out_5, addernor_5_out_4, addernor_5_out_5, addernor_6_out_4, addernor_6_out_5,
       addernor_7_out_4, addernor_7_out_5, addernor_8_out_5, addernor_9_out_4, addernor_9_out_5,
       addernor_10_out_4, addernor_10_out_5, addernor_11_out_4, addernor_11_out_5, addernor_12_out_4,
       addernor_12_out_5, addernor_13_out_4, addernor_13_out_5, addernor_14_out_4, addernor_14_out_5,
       addernor_15_out_5, halfaddernor_1_out_4, halfaddernor_2_out_4, halfaddernor_3_out_4,
       halfaddernor_4_out_4, halfaddernor_5_out_4, mult_1_out_3, mult_2_out_3, mult_3_out_3, mult_4_out_3,
       mult_5_out_3, mult_6_out_3, mult_7_out_3, mult_8_out_3, mult_9_out_3, mult_10_out_3, mult_11_out_3,
       mult_12_out_3, mult_13_out_3, mult_14_out_3, mult_15_out_3, mult_16_out_3, mult_17_out_3,
       mult_18_out_3, mult_19_out_3, mult_20_out_3, mult_21_out_3, mult_23_out_3, mult_24_out_3,
       mult_25_out_3;

  Mult mult_1 (.in_1(b4), .in_2(a4), .out_3(mult_1_out_3));
  Mult mult_2 (.in_1(b3), .in_2(a3), .out_3(mult_2_out_3));
  Mult mult_3 (.in_1(b4), .in_2(a2), .out_3(mult_3_out_3));
  Mult mult_4 (.in_1(b3), .in_2(a4), .out_3(mult_4_out_3));
  Mult mult_5 (.in_1(b4), .in_2(a3), .out_3(mult_5_out_3));
  Mult mult_6 (.in_1(b2), .in_2(a3), .out_3(mult_6_out_3));
  Mult mult_7 (.in_1(b3), .in_2(a2), .out_3(mult_7_out_3));
  Mult mult_8 (.in_1(b4), .in_2(a1), .out_3(mult_8_out_3));
  Mult mult_9 (.in_1(b2), .in_2(a4), .out_3(mult_9_out_3));
  Mult mult_10 (.in_1(b2), .in_2(a2), .out_3(mult_10_out_3));
  Mult mult_11 (.in_1(b3), .in_2(a1), .out_3(mult_11_out_3));
  Mult mult_12 (.in_1(b4), .in_2(a0), .out_3(mult_12_out_3));
  Mult mult_13 (.in_1(b1), .in_2(a4), .out_3(mult_13_out_3));
  AdderNor addernor_1 (.in_1(mult_1_out_3), .in_2(addernor_2_out_5), .in_3(addernor_8_out_5), .out_4(s8), .out_5(s9));
  Mult mult_14 (.in_1(b2), .in_2(a1), .out_3(mult_14_out_3));
  Mult mult_15 (.in_1(b3), .in_2(a0), .out_3(mult_15_out_3));
  Mult mult_16 (.in_1(b0), .in_2(a4), .out_3(mult_16_out_3));
  Mult mult_17 (.in_1(b1), .in_2(a3), .out_3(mult_17_out_3));
  AdderNor addernor_2 (
    .in_1(mult_4_out_3), .in_2(mult_5_out_3), .in_3(addernor_4_out_5), .out_4(addernor_2_out_4),
    .out_5(addernor_2_out_5));
  Mult mult_18 (.in_1(b1), .in_2(a1), .out_3(mult_18_out_3));
  Mult mult_19 (.in_1(b2), .in_2(a0), .out_3(mult_19_out_3));
  Mult mult_20 (.in_1(b0), .in_2(a3), .out_3(mult_20_out_3));
  Mult mult_21 (.in_1(b1), .in_2(a2), .out_3(mult_21_out_3));
  AdderNor addernor_3 (
    .in_1(mult_7_out_3), .in_2(mult_8_out_3), .in_3(addernor_6_out_5), .out_4(addernor_3_out_4),
    .out_5(addernor_3_out_5));
  AdderNor addernor_4 (
    .in_1(mult_9_out_3), .in_2(mult_2_out_3), .in_3(addernor_5_out_5), .out_4(addernor_4_out_4),
    .out_5(addernor_4_out_5));
  Mult mult_22 (.in_1(a0), .in_2(b0), .out_3(s0));
  Mult mult_23 (.in_1(a1), .in_2(b0), .out_3(mult_23_out_3));
  Mult mult_24 (.in_1(b1), .in_2(a0), .out_3(mult_24_out_3));
  Mult mult_25 (.in_1(b0), .in_2(a2), .out_3(mult_25_out_3));
  AdderNor addernor_5 (
    .in_1(mult_13_out_3), .in_2(mult_6_out_3), .in_3(addernor_7_out_5), .out_4(addernor_5_out_4),
    .out_5(addernor_5_out_5));
  AdderNor addernor_6 (
    .in_1(mult_16_out_3), .in_2(mult_17_out_3), .in_3(addernor_9_out_5), .out_4(addernor_6_out_4),
    .out_5(addernor_6_out_5));
  AdderNor addernor_7 (
    .in_1(mult_10_out_3), .in_2(mult_11_out_3), .in_3(addernor_10_out_5), .out_4(addernor_7_out_4),
    .out_5(addernor_7_out_5));
  AdderNor addernor_8 (
    .in_1(addernor_2_out_4), .in_2(addernor_11_out_5), .in_3(addernor_15_out_5), .out_4(s7),
    .out_5(addernor_8_out_5));
  AdderNor addernor_9 (
    .in_1(mult_20_out_3), .in_2(mult_21_out_3), .in_3(addernor_12_out_5), .out_4(addernor_9_out_4),
    .out_5(addernor_9_out_5));
  AdderNor addernor_10 (
    .in_1(mult_14_out_3), .in_2(mult_15_out_3), .in_3(halfaddernor_2_out_4), .out_4(addernor_10_out_4),
    .out_5(addernor_10_out_5));
  AdderNor addernor_11 (
    .in_1(addernor_4_out_4), .in_2(mult_3_out_3), .in_3(addernor_3_out_5), .out_4(addernor_11_out_4),
    .out_5(addernor_11_out_5));
  HalfAdderNor halfaddernor_1 (.in_1(mult_23_out_3), .in_2(mult_24_out_3), .out_3(s1), .out_4(halfaddernor_1_out_4));
  AdderNor addernor_12 (
    .in_1(mult_25_out_3), .in_2(mult_18_out_3), .in_3(halfaddernor_1_out_4), .out_4(addernor_12_out_4),
    .out_5(addernor_12_out_5));
  AdderNor addernor_13 (
    .in_1(addernor_5_out_4), .in_2(addernor_3_out_4), .in_3(addernor_14_out_5), .out_4(addernor_13_out_4),
    .out_5(addernor_13_out_5));
  AdderNor addernor_14 (
    .in_1(addernor_6_out_4), .in_2(addernor_7_out_4), .in_3(halfaddernor_3_out_4), .out_4(addernor_14_out_4),
    .out_5(addernor_14_out_5));
  AdderNor addernor_15 (
    .in_1(addernor_11_out_4), .in_2(halfaddernor_4_out_4), .in_3(addernor_13_out_5), .out_4(s6),
    .out_5(addernor_15_out_5));
  HalfAdderNor halfaddernor_2 (
    .in_1(addernor_12_out_4), .in_2(mult_19_out_3), .out_3(s2), .out_4(halfaddernor_2_out_4));
  HalfAdderNor halfaddernor_3 (
    .in_1(addernor_9_out_4), .in_2(addernor_10_out_4), .out_3(s3), .out_4(halfaddernor_3_out_4));
  HalfAdderNor halfaddernor_4 (
    .in_1(addernor_13_out_4), .in_2(halfaddernor_5_out_4), .out_3(s5), .out_4(halfaddernor_4_out_4));
  HalfAdderNor halfaddernor_5 (
    .in_1(addernor_14_out_4), .in_2(mult_12_out_3), .out_3(s4), .out_4(halfaddernor_5_out_4));
endmodule

module Mult (
  input  in_1,
  input  in_2,
  output out_3
);

  wire nor_1_out, nor_2_out;

  nor nor_1 (nor_1_out, in_1, in_1);
  nor nor_2 (nor_2_out, in_2, in_2);
  nor nor_3 (out_3, nor_1_out, nor_2_out);
endmodule

module HalfAdderNor (
  input  in_1,
  input  in_2,
  output out_3,
  output out_4
);

  wire nor_1_out, nor_2_out, nor_3_out;

  nor nor_1 (nor_1_out, in_1, in_1);
  nor nor_2 (nor_2_out, in_2, in_2);
  nor nor_3 (nor_3_out, in_1, in_2);
  nor nor_4 (out_4, nor_1_out, nor_2_out);
  nor nor_5 (out_3, nor_3_out, out_4);
endmodule

module AdderNor (
  input  in_1,
  input  in_2,
  input  in_3,
  output out_4,
  output out_5
);

  wire nor_1_out, nor_2_out, nor_3_out, nor_4_out, nor_5_out, nor_6_out, nor_7_out;

  nor nor_1 (nor_1_out, in_1, in_2);
  nor nor_2 (nor_2_out, in_1, nor_1_out);
  nor nor_3 (nor_3_out, in_2, nor_1_out);
  nor nor_4 (nor_4_out, nor_2_out, nor_3_out);
  nor nor_5 (nor_5_out, nor_4_out, in_3);
  nor nor_6 (nor_6_out, nor_4_out, nor_5_out);
  nor nor_7 (nor_7_out, in_3, nor_5_out);
  nor nor_8 (out_4, nor_6_out, nor_7_out);
  nor nor_9 (out_5, nor_5_out, nor_1_out);
endmodule
