// Logisim project trabalho.circ as structural Verilog: 4 circuits, main circuit main
module main (
  input  in_1
);

  wire and2portas_1_out_3, and2portas_2_out_3, and2portas_3_out_3, and2portas_4_out_3, and3portas_1_out_4,
       and3portas_2_out_4, and3portas_3_out_4, and3portas_4_out_4, and3portas_5_out_4, and3portas_6_out_4,
       and3portas_7_out_4, and4portas_1_out_5, and_1_out, button_1_out, clock_1_out, d_ff_1_q, d_ff_1_qn,
       d_ff_2_q, d_ff_2_qn, d_ff_3_q, d_ff_3_qn, not_1_out, not_2_out, not_3_out, not_4_out, or_1_out,
       or_2_out, or_3_out, s_r_ff_1_q;

  Button button_1 (.out(button_1_out));
  Clock clock_1 (.out(clock_1_out));
  not not_1 (not_1_out, s_r_ff_1_q);
  not not_2 (not_2_out, in_1);
  S_R_Flip_Flop #(.trigger("high")) s_r_ff_1 (
    .S(button_1_out), .R(and_1_out), .clk(not_2_out), .Q(s_r_ff_1_q));  // open: reset, Qn, preset
  AND3PORTAS and3portas_1 (.in_1(d_ff_1_qn), .in_2(d_ff_2_q), .in_3(d_ff_3_qn), .out_4(and3portas_1_out_4));
  AND4PORTAS and4portas_1 (
    .in_1(d_ff_1_qn), .in_2(d_ff_2_qn), .in_3(not_1_out), .in_4(d_ff_3_q), .out_5(and4portas_1_out_5));
  AND3PORTAS and3portas_2 (.in_1(s_r_ff_1_q), .in_2(d_ff_3_q), .in_3(d_ff_1_qn), .out_4(and3portas_2_out_4));
  or or_1 (or_1_out, and3portas_1_out_4, and4portas_1_out_5);
  AND2PORTAS and2portas_1 (.in_1(d_ff_1_qn), .in_2(d_ff_3_qn), .out_3(and2portas_1_out_3));
  D_Flip_Flop d_ff_1 (.D(and3portas_2_out_4), .clk(clock_1_out), .Q(d_ff_1_q), .Qn(d_ff_1_qn));  // open: preset, reset
  D_Flip_Flop d_ff_2 (.D(or_1_out), .clk(clock_1_out), .Q(d_ff_2_q), .Qn(d_ff_2_qn));  // open: preset, reset
  D_Flip_Flop d_ff_3 (.D(and2portas_1_out_3), .clk(clock_1_out), .Q(d_ff_3_q), .Qn(d_ff_3_qn));  // open: preset, reset
  and and_1 (and_1_out, or_3_out, or_2_out);
  AND3PORTAS and3portas_3 (.in_1(d_ff_1_qn), .in_2(d_ff_2_qn), .in_3(d_ff_3_qn), .out_4(and3portas_3_out_4));
  AND3PORTAS and3portas_4 (.in_1(d_ff_1_qn), .in_2(d_ff_2_qn), .in_3(d_ff_3_q), .out_4(and3portas_4_out_4));
  AND2PORTAS and2portas_2 (.in_1(d_ff_1_qn), .in_2(d_ff_2_q), .out_3(and2portas_2_out_3));
  AND3PORTAS and3portas_5 (.in_1(d_ff_1_q), .in_2(d_ff_2_qn), .in_3(d_ff_3_qn), .out_4(and3portas_5_out_4));
  AND3PORTAS and3portas_6 (.in_1(d_ff_1_qn), .in_2(d_ff_2_q), .in_3(d_ff_3_qn), .out_4(and3portas_6_out_4));
  AND3PORTAS and3portas_7 (.in_1(d_ff_1_qn), .in_2(d_ff_2_q), .in_3(d_ff_3_q), .out_4(and3portas_7_out_4));
  AND2PORTAS and2portas_3 (.in_1(d_ff_1_qn), .in_2(d_ff_2_qn), .out_3(and2portas_3_out_3));
  AND2PORTAS and2portas_4 (.in_1(d_ff_2_qn), .in_2(d_ff_3_qn), .out_3(and2portas_4_out_3));
  or or_2 (or_2_out, and2portas_2_out_3, and3portas_5_out_4);
  or or_3 (or_3_out, and2portas_3_out_3, and2portas_4_out_3);
  LED led_1 (.in(and3portas_3_out_4));
  LED led_2 (.in(and3portas_4_out_4));
  LED led_3 (.in(or_2_out));
  LED led_4 (.in(and3portas_6_out_4));
  LED led_5 (.in(and3portas_7_out_4));
  LED led_6 (.in(or_3_out));
  LED led_7 (.in(and3portas_3_out_4));
  LED led_8 (.in(and3portas_4_out_4));
  LED led_9 (.in(or_2_out));
  not not_3 (not_3_out, and_1_out);
  not not_4 (not_4_out, and_1_out);
  LED led_10 (.in(and_1_out));
  LED led_11 (.in(not_3_out));
  LED led_12 (.in(and_1_out));
  LED led_13 (.in(not_4_out));
endmodule

module AND3PORTAS (
  input  in_1,
  input  in_2,
  input  in_3,
  output out_4
);

  wire and_1_out;

  and and_1 (and_1_out, in_1, in_2);
  and and_2 (out_4, and_1_out, in_3);
endmodule

module AND4PORTAS (
  input  in_1,
  input  in_2,
  input  in_3,
  input  in_4,
  output out_5
);

  wire and_1_out, and_2_out;

  and and_1 (and_1_out, in_1, in_2);
  and and_2 (and_2_out, in_3, in_4);
  and and_3 (out_5, and_1_out, and_2_out);
endmodule

module AND2PORTAS (
  input  in_1,
  input  in_2,
  output out_3
);

  and and_1 (out_3, in_1, in_2);
endmodule
