// Logisim project multiplicador_5bits.circ as structural Verilog: 3 circuits, main circuit main
module main (
  input  b4,
  input  b3,
  input  b2,
  input  b1,
  input  b0,
  input  a4,
  input  a3,
  input  a2,
  input  a1,
  input  a0
);

  wire multiplicador_1_s0, multiplicador_1_s1, multiplicador_1_s2, multiplicador_1_s3, multiplicador_1_s4,
       multiplicador_1_s5, multiplicador_1_s6, multiplicador_1_s7, multiplicador_1_s8, multiplicador_1_s9;

  LED s9 (.in(multiplicador_1_s9));
  LED s8 (.in(multiplicador_1_s8));
  LED s7 (.in(multiplicador_1_s7));
  LED s6 (.in(multiplicador_1_s6));
  LED s5 (.in(multiplicador_1_s5));
  LED s4 (.in(multiplicador_1_s4));
  multiplicador multiplicador_1 (
    .s0(multiplicador_1_s0), .s1(multiplicador_1_s1), .s2(multiplicador_1_s2), .s3(multiplicador_1_s3),
    .s4(multiplicador_1_s4), .s5(multiplicador_1_s5), .s6(multiplicador_1_s6), .s7(multiplicador_1_s7),
    .s8(multiplicador_1_s8), .s9(multiplicador_1_s9), .a0(a0), .a1(a1), .a2(a2), .a3(a3), .a4(a4), .b0(b0),
    .b1(b1), .b2(b2), .b3(b3), .b4(b4));
  LED s3 (.in(multiplicador_1_s3));
  LED s2 (.in(multiplicador_1_s2));
  LED s1 (.in(multiplicador_1_s1));
  LED s0 (.in(multiplicador_1_s0));
endmodule

module multiplicador (
  input  a0,
  input  a1,
  input  a2,
  input  a3,
  input  a4,
  input  b0,
  input  b1,
  input  b2,
  input  b3,
  input  b4,
  output s0,
  output s1,
  output s2,
  output s3,
  output s4,
  output s5,
  output s6,
  output s7,
  output s8,
  output s9
);

  wire undriven, undriven_2, undriven_3, undriven_4, undriven_5, undriven_6, undriven_7, undriven_8,
       undriven_9, undriven_10, undriven_11, undriven_12, undriven_13, undriven_14, undriven_15, undriven_16,
       undriven_17, undriven_18, undriven_19, undriven_20, undriven_21, undriven_22, undriven_23,
       undriven_24, undriven_25;

  Mult mult_1 (.in_1(a0), .in_2(b0), .in_3(undriven_23));
  Mult mult_2 (.in_1(a1), .in_2(b0), .in_3(undriven_24));
  Mult mult_3 (.in_1(b1), .in_2(a0), .in_3(undriven_25));
  Mult mult_4 (.in_1(b0), .in_2(a2), .in_3(undriven_22));
  Mult mult_5 (.in_1(b1), .in_2(a1), .in_3(undriven_21));
  Mult mult_6 (.in_1(b2), .in_2(a0), .in_3(undriven_20));
  Mult mult_7 (.in_1(b0), .in_2(a3), .in_3(undriven_19));
  Mult mult_8 (.in_1(b1), .in_2(a2), .in_3(undriven_18));
  Mult mult_9 (.in_1(b2), .in_2(a1), .in_3(undriven_17));
  Mult mult_10 (.in_1(b3), .in_2(a0), .in_3(undriven_16));
  Mult mult_11 (.in_1(b0), .in_2(a4), .in_3(undriven_15));
  Mult mult_12 (.in_1(b1), .in_2(a3), .in_3(undriven_14));
  Mult mult_13 (.in_1(b2), .in_2(a2), .in_3(undriven_13));
  Mult mult_14 (.in_1(b3), .in_2(a1), .in_3(undriven_12));
  Mult mult_15 (.in_1(b4), .in_2(a0), .in_3(undriven_11));
  Mult mult_16 (.in_1(b1), .in_2(a4), .in_3(undriven_10));
  Mult mult_17 (.in_1(b2), .in_2(a3), .in_3(undriven_9));
  Mult mult_18 (.in_1(b3), .in_2(a2), .in_3(undriven_8));
  Mult mult_19 (.in_1(b4), .in_2(a1), .in_3(undriven_7));
  Mult mult_20 (.in_1(b2), .in_2(a4), .in_3(undriven_6));
  Mult mult_21 (.in_1(b3), .in_2(a3), .in_3(undriven_5));
  Mult mult_22 (.in_1(b4), .in_2(a2), .in_3(undriven_4));
  Mult mult_23 (.in_1(b3), .in_2(a4), .in_3(undriven_3));
  Mult mult_24 (.in_1(b4), .in_2(a3), .in_3(undriven_2));
  Mult mult_25 (.in_1(b4), .in_2(a4), .in_3(undriven));
endmodule

module Mult (
  input  in_1,
  input  in_2,
  input  in_3
);

  wire nor_1_out, nor_2_out, nor_3_out;

  nor nor_1 (nor_1_out, in_1, in_1);
  nor nor_2 (nor_2_out, in_3, in_3);
  nor nor_3 (nor_3_out, nor_1_out, nor_2_out);
endmodule
