// Logisim project processador.circ as structural Verilog: 14 circuits, main circuit main
module main (
  input  in_1,
  output [31:0] out_2,
  output out_3
);

  wire clok, enable_display, jump, multiplexer_1_out, seletor_mux_cte, seletor_zero_jump, todo_mundo_zero,
       write_enable;
  wire [2:0] seletor_ula;
  wire [3:0] a, b, c, op;
  wire [15:0] cte_mux;
  wire [31:0] banco_registradores_1_a, banco_registradores_1_b, bit_extender_1_out, cte, multiplexer_2_out,
       multiplexer_3_out, register_1_q, somador_carry_look_ahead_1_resultado,
       subtrator_complemento_de_dois_1_out_3, ula_1_out_5;

  Multiplexer multiplexer_1 (.in0(jump), .in1(todo_mundo_zero), .out(multiplexer_1_out), .sel(seletor_zero_jump));
  Multiplexer #(.width(32)) multiplexer_2 (.in0(32'h1), .in1(cte), .out(multiplexer_2_out), .sel(multiplexer_1_out));
  banco_registradores banco_registradores_1 (
    .cezao(ula_1_out_5), .enable_write(write_enable), .cezinho(c), .clock(clok), .azinho(a), .in_6(in_1),
    .bezinho(b), .A(banco_registradores_1_a), .B(banco_registradores_1_b));
  assign bit_extender_1_out = {{16{1'b0}}, cte_mux};  // Bit_Extender bit_extender_1
  assign cte = {{16{cte_mux[15]}}, cte_mux};  // Bit_Extender bit_extender_2
  Multiplexer #(.width(32)) multiplexer_3 (
    .in0(banco_registradores_1_b), .in1(bit_extender_1_out), .out(multiplexer_3_out), .sel(seletor_mux_cte));
  somador_carry_look_ahead somador_carry_look_ahead_1 (
    .carry_in(1'b0), .A({{10{register_1_q[31]}}, register_1_q[21:0]}), .B(multiplexer_2_out),
    .resultado(somador_carry_look_ahead_1_resultado));
  Clock clock_1 (.out(clok));
  Register #(.width(32)) register_1 (
    .D(somador_carry_look_ahead_1_resultado), .en(1'b1), .clk(clok),
    .Q({{10{register_1_q[31]}}, register_1_q[21:0]}), .clr(in_1));
  ROM #(.addrWidth(22), .dataWidth(32)) rom_1 (.addr(register_1_q[21:0]), .data({cte_mux, c, b, a, op}));
  subtrator_complemento_de_dois subtrator_complemento_de_dois_1 (
    .A(banco_registradores_1_a), .B(banco_registradores_1_b), .out_3(subtrator_complemento_de_dois_1_out_3));
  ULA ula_1 (
    .A(banco_registradores_1_a), .B(multiplexer_3_out), .Seletor(seletor_ula), .zeros(out_3),
    .out_5(ula_1_out_5));
  todos_zeros todos_zeros_1 (.resultado(subtrator_complemento_de_dois_1_out_3), .tudo_zero(todo_mundo_zero));
  Register #(.width(32)) register_2 (
    .D(banco_registradores_1_a), .en(enable_display), .clk(clok), .Q(out_2));  // open: clr
  memoria_de_controle memoria_de_controle_1 (
    .op(op), .seletor_ula(seletor_ula), .seletor_cte_ula(seletor_mux_cte),
    .write_enable_banco_registradores(write_enable), .enable_display(enable_display), .jump(jump),
    .Zeros(seletor_zero_jump));
  // also tied to GND on the sheet: register_1_q[31]

  // Other names for the same wires on the sheet: clear = in_1

  // Notes on the sheet:
  //   contents of rom_1 (hex, n*v repeats v):
  //   12341230 3454210 ffff0000 1102b 1202b 2303b 4311 5211 6321 4c 5c 6c 7542 8562 9642 7c 8c 9c fa00b
  //   eb00b cab3 cc cab4 cc cab5 cc c0c6 cc c0c7 cc c0c8 cc 3f049 fc 8f04a fc 8f0fb fc c 1c 2c 3c 4c 5c 6c
  //   7c 2000d 0 2000d 0 3000d 0 0 2087e 0 2098e f
endmodule

module memoria_de_controle (
  input  [3:0] op,
  output [2:0] seletor_ula,
  output seletor_cte_ula,
  output write_enable_banco_registradores,
  output enable_display,
  output jump,
  output Zeros
);

  ROM #(.addrWidth(4)) rom_1 (
    .addr(op),
    .data({Zeros, jump, enable_display, write_enable_banco_registradores, seletor_cte_ula, seletor_ula}));

  // Notes on the sheet:
  //   00 10 11 12 13 14 15 16
  //   17 1b 1c 18 20 40 81 40
  //   contents of rom_1 (hex, n*v repeats v):
  //   0 10 11 12 13 14 15 16 17 1b 1c 18 20 40 81 40
endmodule

module banco_registradores (
  input  [31:0] cezao,
  input  enable_write,
  input  [3:0] cezinho,
  input  clock,
  input  [3:0] azinho,
  input  in_6,
  input  [3:0] bezinho,
  output [31:0] A,
  output [31:0] B
);

  wire demultiplexer_1_out0, demultiplexer_1_out1, demultiplexer_1_out2, demultiplexer_1_out3,
       demultiplexer_1_out4, demultiplexer_1_out5, demultiplexer_1_out6, demultiplexer_1_out7,
       demultiplexer_1_out8, demultiplexer_1_out9, demultiplexer_1_out10, demultiplexer_1_out11,
       demultiplexer_1_out12, demultiplexer_1_out13, demultiplexer_1_out14, demultiplexer_1_out15;
  wire [31:0] register_1_q, register_2_q, register_3_q, register_4_q, register_5_q, register_6_q,
       register_7_q, register_8_q, register_9_q, register_10_q, register_11_q, register_12_q, register_13_q,
       register_14_q, register_15_q, register_16_q;

  Demultiplexer #(.select(4)) demultiplexer_1 (
    .out0(demultiplexer_1_out0), .out1(demultiplexer_1_out1), .out2(demultiplexer_1_out2),
    .out3(demultiplexer_1_out3), .out4(demultiplexer_1_out4), .out5(demultiplexer_1_out5),
    .out6(demultiplexer_1_out6), .out7(demultiplexer_1_out7), .out8(demultiplexer_1_out8),
    .out9(demultiplexer_1_out9), .out10(demultiplexer_1_out10), .out11(demultiplexer_1_out11),
    .out12(demultiplexer_1_out12), .out13(demultiplexer_1_out13), .out14(demultiplexer_1_out14),
    .out15(demultiplexer_1_out15), .in(enable_write), .sel(cezinho));
  Register #(.width(32)) register_1 (
    .D({32{1'b0}}), .en(demultiplexer_1_out0), .clk(clock), .Q(register_1_q), .clr(in_6));
  Register #(.width(32)) register_2 (.D(cezao), .en(demultiplexer_1_out1), .clk(clock), .Q(register_2_q), .clr(in_6));
  Register #(.width(32)) register_3 (.D(cezao), .en(demultiplexer_1_out2), .clk(clock), .Q(register_3_q), .clr(in_6));
  Register #(.width(32)) register_4 (.D(cezao), .en(demultiplexer_1_out3), .clk(clock), .Q(register_4_q), .clr(in_6));
  Register #(.width(32)) register_5 (.D(cezao), .en(demultiplexer_1_out4), .clk(clock), .Q(register_5_q), .clr(in_6));
  Register #(.width(32)) register_6 (.D(cezao), .en(demultiplexer_1_out5), .clk(clock), .Q(register_6_q), .clr(in_6));
  Register #(.width(32)) register_7 (.D(cezao), .en(demultiplexer_1_out6), .clk(clock), .Q(register_7_q), .clr(in_6));
  Register #(.width(32)) register_8 (.D(cezao), .en(demultiplexer_1_out7), .clk(clock), .Q(register_8_q), .clr(in_6));
  Register #(.width(32)) register_9 (.D(cezao), .en(demultiplexer_1_out8), .clk(clock), .Q(register_9_q), .clr(in_6));
  Register #(.width(32)) register_10 (.D(cezao), .en(demultiplexer_1_out9), .clk(clock), .Q(register_10_q), .clr(in_6));
  Register #(.width(32)) register_11 (
    .D(cezao), .en(demultiplexer_1_out10), .clk(clock), .Q(register_11_q), .clr(in_6));
  Register #(.width(32)) register_12 (
    .D(cezao), .en(demultiplexer_1_out11), .clk(clock), .Q(register_12_q), .clr(in_6));
  Register #(.width(32)) register_13 (
    .D(cezao), .en(demultiplexer_1_out12), .clk(clock), .Q(register_13_q), .clr(in_6));
  Register #(.width(32)) register_14 (
    .D(cezao), .en(demultiplexer_1_out13), .clk(clock), .Q(register_14_q), .clr(in_6));
  Register #(.width(32)) register_15 (
    .D(cezao), .en(demultiplexer_1_out14), .clk(clock), .Q(register_15_q), .clr(in_6));
  Register #(.width(32)) register_16 (
    .D(cezao), .en(demultiplexer_1_out15), .clk(clock), .Q(register_16_q), .clr(in_6));
  Multiplexer #(.select(4), .width(32)) multiplexer_1 (
    .in0(register_1_q), .in1(register_2_q), .in2(register_3_q), .in3(register_4_q), .in4(register_5_q),
    .in5(register_6_q), .in6(register_7_q), .in7(register_8_q), .in8(register_9_q), .in9(register_10_q),
    .in10(register_11_q), .in11(register_12_q), .in12(register_13_q), .in13(register_14_q),
    .in14(register_15_q), .in15(register_16_q), .out(A), .sel(azinho));
  Multiplexer #(.select(4), .width(32)) multiplexer_2 (
    .in0(register_1_q), .in1(register_2_q), .in2(register_3_q), .in3(register_4_q), .in4(register_5_q),
    .in5(register_6_q), .in6(register_7_q), .in7(register_8_q), .in8(register_9_q), .in9(register_10_q),
    .in10(register_11_q), .in11(register_12_q), .in12(register_13_q), .in13(register_14_q),
    .in14(register_15_q), .in15(register_16_q), .out(B), .sel(bezinho));
endmodule

module ULA (
  input  [31:0] A,
  input  [31:0] B,
  input  [2:0] Seletor,
  output zeros,
  output [31:0] out_5
);

  wire [31:0] and_ula_1_out_3, deslocador_direita_1_b, deslocador_esquerda_1_b, not_ula_1_out_2,
       or_ula_1_out_3, somador_carry_look_ahead_1_resultado, subtrator_complemento_de_dois_1_out_3,
       xor_ula_1_out_3;

  somador_carry_look_ahead somador_carry_look_ahead_1 (
    .carry_in(1'b0), .A(A), .B(B), .resultado(somador_carry_look_ahead_1_resultado));
  subtrator_complemento_de_dois subtrator_complemento_de_dois_1 (
    .A(A), .B(B), .out_3(subtrator_complemento_de_dois_1_out_3));
  and_ula and_ula_1 (.A(A), .B(B), .out_3(and_ula_1_out_3));
  or_ula or_ula_1 (.A(A), .B(B), .out_3(or_ula_1_out_3));
  xor_ula xor_ula_1 (.A(A), .B(B), .out_3(xor_ula_1_out_3));
  not_ula not_ula_1 (.A(A), .out_2(not_ula_1_out_2));
  deslocador_esquerda deslocador_esquerda_1 (.A(A), .B(deslocador_esquerda_1_b));
  deslocador_direita deslocador_direita_1 (.A(A), .B(deslocador_direita_1_b));
  Multiplexer #(.select(3), .width(32)) multiplexer_1 (
    .in0(somador_carry_look_ahead_1_resultado), .in1(subtrator_complemento_de_dois_1_out_3),
    .in2(and_ula_1_out_3), .in3(or_ula_1_out_3), .in4(xor_ula_1_out_3), .in5(not_ula_1_out_2),
    .in6(deslocador_esquerda_1_b), .in7(deslocador_direita_1_b), .out(out_5), .sel(Seletor));
  todos_zeros todos_zeros_1 (.resultado(out_5), .tudo_zero(zeros));
endmodule

module somador_carry_look_ahead (
  input  carry_in,
  input  [31:0] A,
  input  [31:0] B,
  output [31:0] resultado
);

  wire modulo_carry_look_ahead_4_bits_1_c_out, modulo_carry_look_ahead_4_bits_2_c_out,
       modulo_carry_look_ahead_4_bits_3_c_out, modulo_carry_look_ahead_4_bits_4_c_out,
       modulo_carry_look_ahead_4_bits_5_c_out, modulo_carry_look_ahead_4_bits_6_c_out,
       modulo_carry_look_ahead_4_bits_7_c_out, modulo_carry_look_ahead_4_bits_8_c_out;

  modulo_carry_look_ahead_4_bits modulo_carry_look_ahead_4_bits_1 (
    .a0(A[0]), .b0(B[0]), .a1(A[1]), .b1(B[1]), .a2(A[2]), .b2(B[2]), .a3(A[3]), .b3(B[3]), .C_in(carry_in),
    .C_out(modulo_carry_look_ahead_4_bits_1_c_out), .s0(resultado[0]), .s1(resultado[1]), .s2(resultado[2]),
    .s3(resultado[3]));
  modulo_carry_look_ahead_4_bits modulo_carry_look_ahead_4_bits_2 (
    .a0(A[16]), .b0(B[16]), .a1(A[17]), .b1(B[17]), .a2(A[18]), .b2(B[18]), .a3(A[19]), .b3(B[19]),
    .C_in(modulo_carry_look_ahead_4_bits_7_c_out), .C_out(modulo_carry_look_ahead_4_bits_2_c_out),
    .s0(resultado[16]), .s1(resultado[17]), .s2(resultado[18]), .s3(resultado[19]));
  modulo_carry_look_ahead_4_bits modulo_carry_look_ahead_4_bits_3 (
    .a0(A[4]), .b0(B[4]), .a1(A[5]), .b1(B[5]), .a2(A[6]), .b2(B[6]), .a3(A[7]), .b3(B[7]),
    .C_in(modulo_carry_look_ahead_4_bits_1_c_out), .C_out(modulo_carry_look_ahead_4_bits_3_c_out),
    .s0(resultado[4]), .s1(resultado[5]), .s2(resultado[6]), .s3(resultado[7]));
  modulo_carry_look_ahead_4_bits modulo_carry_look_ahead_4_bits_4 (
    .a0(A[20]), .b0(B[20]), .a1(A[21]), .b1(B[21]), .a2(A[22]), .b2(B[22]), .a3(A[23]), .b3(B[23]),
    .C_in(modulo_carry_look_ahead_4_bits_2_c_out), .C_out(modulo_carry_look_ahead_4_bits_4_c_out),
    .s0(resultado[20]), .s1(resultado[21]), .s2(resultado[22]), .s3(resultado[23]));
  modulo_carry_look_ahead_4_bits modulo_carry_look_ahead_4_bits_5 (
    .a0(A[8]), .b0(B[8]), .a1(A[9]), .b1(B[9]), .a2(A[10]), .b2(B[10]), .a3(A[11]), .b3(B[11]),
    .C_in(modulo_carry_look_ahead_4_bits_3_c_out), .C_out(modulo_carry_look_ahead_4_bits_5_c_out),
    .s0(resultado[8]), .s1(resultado[9]), .s2(resultado[10]), .s3(resultado[11]));
  modulo_carry_look_ahead_4_bits modulo_carry_look_ahead_4_bits_6 (
    .a0(A[24]), .b0(B[24]), .a1(A[25]), .b1(B[25]), .a2(A[26]), .b2(B[26]), .a3(A[27]), .b3(B[27]),
    .C_in(modulo_carry_look_ahead_4_bits_4_c_out), .C_out(modulo_carry_look_ahead_4_bits_6_c_out),
    .s0(resultado[24]), .s1(resultado[25]), .s2(resultado[26]), .s3(resultado[27]));
  modulo_carry_look_ahead_4_bits modulo_carry_look_ahead_4_bits_7 (
    .a0(A[12]), .b0(B[12]), .a1(A[13]), .b1(B[13]), .a2(A[14]), .b2(B[14]), .a3(A[15]), .b3(B[15]),
    .C_in(modulo_carry_look_ahead_4_bits_5_c_out), .C_out(modulo_carry_look_ahead_4_bits_7_c_out),
    .s0(resultado[12]), .s1(resultado[13]), .s2(resultado[14]), .s3(resultado[15]));
  modulo_carry_look_ahead_4_bits modulo_carry_look_ahead_4_bits_8 (
    .a0(A[28]), .b0(B[28]), .a1(A[29]), .b1(B[29]), .a2(A[30]), .b2(B[30]), .a3(A[31]), .b3(B[31]),
    .C_in(modulo_carry_look_ahead_4_bits_6_c_out), .C_out(modulo_carry_look_ahead_4_bits_8_c_out),
    .s0(resultado[28]), .s1(resultado[29]), .s2(resultado[30]), .s3(resultado[31]));
  // also tied to GND on the sheet: modulo_carry_look_ahead_4_bits_8_c_out
endmodule

module modulo_carry_look_ahead_4_bits (
  input  a0,
  input  b0,
  input  a1,
  input  b1,
  input  a2,
  input  b2,
  input  a3,
  input  b3,
  input  C_in,
  output C_out,
  output s0,
  output s1,
  output s2,
  output s3
);

  wire and_1_out, and_2_out, and_3_out, and_4_out, and_5_out, and_6_out, and_7_out, and_8_out, and_9_out,
       and_10_out, and_11_out, and_12_out, and_13_out, and_14_out, and_15_out, and_16_out, and_17_out,
       and_18_out, and_19_out, and_20_out, and_21_out, and_22_out, and_23_out, and_24_out, or_1_out,
       or_2_out, or_3_out, or_4_out, or_6_out, or_7_out, or_8_out, or_9_out, or_10_out, or_11_out, or_12_out,
       or_13_out, or_14_out, xor_1_out, xor_3_out, xor_5_out, xor_7_out;

  and and_1 (and_1_out, a0, b0);
  and and_2 (and_2_out, or_1_out, or_6_out);
  and and_3 (and_3_out, and_2_out, or_8_out);
  and and_4 (and_4_out, and_3_out, or_11_out);
  or or_1 (or_1_out, a0, b0);
  and and_5 (and_5_out, and_1_out, or_6_out);
  and and_6 (and_6_out, and_4_out, C_in);
  and and_7 (and_7_out, and_5_out, or_8_out);
  and and_8 (and_8_out, and_7_out, or_11_out);
  or or_2 (or_2_out, and_6_out, and_8_out);
  and and_9 (and_9_out, and_11_out, or_8_out);
  and and_10 (and_10_out, and_9_out, or_11_out);
  or or_3 (or_3_out, or_2_out, and_10_out);
  or or_4 (or_4_out, or_3_out, and_12_out);
  or or_5 (C_out, or_4_out, and_20_out);
  and and_11 (and_11_out, a1, b1);
  or or_6 (or_6_out, a1, b1);
  and and_12 (and_12_out, and_16_out, or_11_out);
  and and_13 (and_13_out, or_1_out, or_6_out);
  and and_14 (and_14_out, and_13_out, or_8_out);
  and and_15 (and_15_out, and_14_out, C_in);
  and and_16 (and_16_out, a2, b2);
  and and_17 (and_17_out, and_1_out, or_6_out);
  and and_18 (and_18_out, and_17_out, or_8_out);
  or or_7 (or_7_out, and_15_out, and_18_out);
  or or_8 (or_8_out, a2, b2);
  and and_19 (and_19_out, and_11_out, or_8_out);
  or or_9 (or_9_out, or_7_out, and_19_out);
  or or_10 (or_10_out, or_9_out, and_16_out);
  xor xor_1 (xor_1_out, C_in, or_1_out);
  xor xor_2 (s0, xor_1_out, and_1_out);
  and and_20 (and_20_out, a3, b3);
  and and_21 (and_21_out, or_1_out, or_6_out);
  and and_22 (and_22_out, and_21_out, C_in);
  or or_11 (or_11_out, a3, b3);
  and and_23 (and_23_out, and_1_out, or_6_out);
  or or_12 (or_12_out, and_22_out, and_23_out);
  or or_13 (or_13_out, or_12_out, and_11_out);
  xor xor_3 (xor_3_out, or_14_out, and_11_out);
  xor xor_4 (s1, xor_3_out, or_6_out);
  and and_24 (and_24_out, or_1_out, C_in);
  or or_14 (or_14_out, and_24_out, and_1_out);
  xor xor_5 (xor_5_out, or_13_out, and_16_out);
  xor xor_6 (s2, xor_5_out, or_8_out);
  xor xor_7 (xor_7_out, or_10_out, and_20_out);
  xor xor_8 (s3, xor_7_out, or_11_out);
endmodule

module subtrator_complemento_de_dois (
  input  [31:0] A,
  input  [31:0] B,
  output [31:0] out_3
);

  wire [31:0] not_ula_1_out_2;

  not_ula not_ula_1 (.A(B), .out_2(not_ula_1_out_2));
  somador_carry_look_ahead somador_carry_look_ahead_1 (.carry_in(1'b1), .A(A), .B(not_ula_1_out_2), .resultado(out_3));
endmodule

module and_ula (
  input  [31:0] A,
  input  [31:0] B,
  output [31:0] out_3
);

  and and_1 (out_3[12], A[12], B[12]);
  and and_2 (out_3[13], A[13], B[13]);
  and and_3 (out_3[14], A[14], B[14]);
  and and_4 (out_3[15], A[15], B[15]);
  and and_5 (out_3[0], A[0], B[0]);
  and and_6 (out_3[1], A[1], B[1]);
  and and_7 (out_3[2], A[2], B[2]);
  and and_8 (out_3[3], A[3], B[3]);
  and and_9 (out_3[4], A[4], B[4]);
  and and_10 (out_3[5], A[5], B[5]);
  and and_11 (out_3[6], A[6], B[6]);
  and and_12 (out_3[7], A[7], B[7]);
  and and_13 (out_3[8], A[8], B[8]);
  and and_14 (out_3[9], A[9], B[9]);
  and and_15 (out_3[10], A[10], B[10]);
  and and_16 (out_3[11], A[11], B[11]);
  and and_17 (out_3[16], A[16], B[16]);
  and and_18 (out_3[17], A[17], B[17]);
  and and_19 (out_3[18], A[18], B[18]);
  and and_20 (out_3[19], A[19], B[19]);
  and and_21 (out_3[20], A[20], B[20]);
  and and_22 (out_3[21], A[21], B[21]);
  and and_23 (out_3[22], A[22], B[22]);
  and and_24 (out_3[23], A[23], B[23]);
  and and_25 (out_3[24], A[24], B[24]);
  and and_26 (out_3[25], A[25], B[25]);
  and and_27 (out_3[26], A[26], B[26]);
  and and_28 (out_3[27], A[27], B[27]);
  and and_29 (out_3[28], A[28], B[28]);
  and and_30 (out_3[29], A[29], B[29]);
  and and_31 (out_3[30], A[30], B[30]);
  and and_32 (out_3[31], A[31], B[31]);
endmodule

module or_ula (
  input  [31:0] A,
  input  [31:0] B,
  output [31:0] out_3
);

  or or_1 (out_3[12], A[12], B[12]);
  or or_2 (out_3[13], A[13], B[13]);
  or or_3 (out_3[14], A[14], B[14]);
  or or_4 (out_3[15], A[15], B[15]);
  or or_5 (out_3[0], A[0], B[0]);
  or or_6 (out_3[1], A[1], B[1]);
  or or_7 (out_3[2], A[2], B[2]);
  or or_8 (out_3[3], A[3], B[3]);
  or or_9 (out_3[4], A[4], B[4]);
  or or_10 (out_3[5], A[5], B[5]);
  or or_11 (out_3[6], A[6], B[6]);
  or or_12 (out_3[7], A[7], B[7]);
  or or_13 (out_3[8], A[8], B[8]);
  or or_14 (out_3[9], A[9], B[9]);
  or or_15 (out_3[10], A[10], B[10]);
  or or_16 (out_3[11], A[11], B[11]);
  or or_17 (out_3[16], A[16], B[16]);
  or or_18 (out_3[17], A[17], B[17]);
  or or_19 (out_3[18], A[18], B[18]);
  or or_20 (out_3[19], A[19], B[19]);
  or or_21 (out_3[20], A[20], B[20]);
  or or_22 (out_3[21], A[21], B[21]);
  or or_23 (out_3[22], A[22], B[22]);
  or or_24 (out_3[23], A[23], B[23]);
  or or_25 (out_3[24], A[24], B[24]);
  or or_26 (out_3[25], A[25], B[25]);
  or or_27 (out_3[26], A[26], B[26]);
  or or_28 (out_3[27], A[27], B[27]);
  or or_29 (out_3[28], A[28], B[28]);
  or or_30 (out_3[29], A[29], B[29]);
  or or_31 (out_3[30], A[30], B[30]);
  or or_32 (out_3[31], A[31], B[31]);
endmodule

module xor_ula (
  input  [31:0] A,
  input  [31:0] B,
  output [31:0] out_3
);

  xor xor_1 (out_3[12], A[12], B[12]);
  xor xor_2 (out_3[13], A[13], B[13]);
  xor xor_3 (out_3[14], A[14], B[14]);
  xor xor_4 (out_3[15], A[15], B[15]);
  xor xor_5 (out_3[0], A[0], B[0]);
  xor xor_6 (out_3[1], A[1], B[1]);
  xor xor_7 (out_3[2], A[2], B[2]);
  xor xor_8 (out_3[3], A[3], B[3]);
  xor xor_9 (out_3[4], A[4], B[4]);
  xor xor_10 (out_3[5], A[5], B[5]);
  xor xor_11 (out_3[6], A[6], B[6]);
  xor xor_12 (out_3[7], A[7], B[7]);
  xor xor_13 (out_3[8], A[8], B[8]);
  xor xor_14 (out_3[9], A[9], B[9]);
  xor xor_15 (out_3[10], A[10], B[10]);
  xor xor_16 (out_3[11], A[11], B[11]);
  xor xor_17 (out_3[16], A[16], B[16]);
  xor xor_18 (out_3[17], A[17], B[17]);
  xor xor_19 (out_3[18], A[18], B[18]);
  xor xor_20 (out_3[19], A[19], B[19]);
  xor xor_21 (out_3[20], A[20], B[20]);
  xor xor_22 (out_3[21], A[21], B[21]);
  xor xor_23 (out_3[22], A[22], B[22]);
  xor xor_24 (out_3[23], A[23], B[23]);
  xor xor_25 (out_3[24], A[24], B[24]);
  xor xor_26 (out_3[25], A[25], B[25]);
  xor xor_27 (out_3[26], A[26], B[26]);
  xor xor_28 (out_3[27], A[27], B[27]);
  xor xor_29 (out_3[28], A[28], B[28]);
  xor xor_30 (out_3[29], A[29], B[29]);
  xor xor_31 (out_3[30], A[30], B[30]);
  xor xor_32 (out_3[31], A[31], B[31]);
endmodule

module not_ula (
  input  [31:0] A,
  output [31:0] out_2
);

  not not_1 (out_2[0], A[0]);
  not not_2 (out_2[4], A[4]);
  not not_3 (out_2[8], A[8]);
  not not_4 (out_2[12], A[12]);
  not not_5 (out_2[16], A[16]);
  not not_6 (out_2[20], A[20]);
  not not_7 (out_2[24], A[24]);
  not not_8 (out_2[28], A[28]);
  not not_9 (out_2[1], A[1]);
  not not_10 (out_2[2], A[2]);
  not not_11 (out_2[5], A[5]);
  not not_12 (out_2[6], A[6]);
  not not_13 (out_2[9], A[9]);
  not not_14 (out_2[10], A[10]);
  not not_15 (out_2[13], A[13]);
  not not_16 (out_2[14], A[14]);
  not not_17 (out_2[17], A[17]);
  not not_18 (out_2[18], A[18]);
  not not_19 (out_2[21], A[21]);
  not not_20 (out_2[22], A[22]);
  not not_21 (out_2[25], A[25]);
  not not_22 (out_2[26], A[26]);
  not not_23 (out_2[29], A[29]);
  not not_24 (out_2[30], A[30]);
  not not_25 (out_2[3], A[3]);
  not not_26 (out_2[7], A[7]);
  not not_27 (out_2[11], A[11]);
  not not_28 (out_2[15], A[15]);
  not not_29 (out_2[19], A[19]);
  not not_30 (out_2[23], A[23]);
  not not_31 (out_2[27], A[27]);
  not not_32 (out_2[31], A[31]);
endmodule

module deslocador_esquerda (
  input  [31:0] A,
  output [31:0] B
);


  assign B = {A[30:0], 1'b0};
  // also tied to GND on the sheet: A[31]
endmodule

module deslocador_direita (
  input  [31:0] A,
  output [31:0] B
);


  assign B = {1'b0, A[31:1]};
  // also tied to GND on the sheet: A[0]
endmodule

module todos_zeros (
  input  [31:0] resultado,
  output tudo_zero
);

  wire and_1_out, and_2_out, and_3_out, and_4_out, and_5_out, and_6_out, and_7_out, and_8_out, and_9_out,
       and_10_out, and_11_out, and_12_out, and_13_out, and_14_out, and_15_out, and_16_out, and_17_out,
       and_18_out, and_19_out, and_20_out, and_21_out, and_22_out, and_23_out, and_24_out, and_25_out,
       and_26_out, and_27_out, and_29_out, and_30_out, and_31_out, not_1_out, not_2_out, not_3_out,
       not_4_out, not_5_out, not_6_out, not_7_out, not_8_out, not_9_out, not_10_out, not_11_out, not_12_out,
       not_13_out, not_14_out, not_15_out, not_16_out, not_17_out, not_18_out, not_19_out, not_20_out,
       not_21_out, not_22_out, not_23_out, not_24_out, not_25_out, not_26_out, not_27_out, not_28_out,
       not_29_out, not_30_out, not_31_out, not_32_out;

  not not_1 (not_1_out, resultado[0]);
  not not_2 (not_2_out, resultado[1]);
  not not_3 (not_3_out, resultado[2]);
  not not_4 (not_4_out, resultado[3]);
  not not_5 (not_5_out, resultado[4]);
  not not_6 (not_6_out, resultado[5]);
  not not_7 (not_7_out, resultado[6]);
  not not_8 (not_8_out, resultado[7]);
  not not_9 (not_9_out, resultado[8]);
  not not_10 (not_10_out, resultado[9]);
  not not_11 (not_11_out, resultado[10]);
  not not_12 (not_12_out, resultado[11]);
  not not_13 (not_13_out, resultado[12]);
  not not_14 (not_14_out, resultado[13]);
  not not_15 (not_15_out, resultado[14]);
  not not_16 (not_16_out, resultado[15]);
  not not_17 (not_17_out, resultado[16]);
  not not_18 (not_18_out, resultado[17]);
  not not_19 (not_19_out, resultado[18]);
  not not_20 (not_20_out, resultado[19]);
  not not_21 (not_21_out, resultado[20]);
  not not_22 (not_22_out, resultado[21]);
  not not_23 (not_23_out, resultado[22]);
  not not_24 (not_24_out, resultado[23]);
  not not_25 (not_25_out, resultado[24]);
  not not_26 (not_26_out, resultado[25]);
  not not_27 (not_27_out, resultado[26]);
  not not_28 (not_28_out, resultado[27]);
  not not_29 (not_29_out, resultado[28]);
  not not_30 (not_30_out, resultado[29]);
  not not_31 (not_31_out, resultado[30]);
  not not_32 (not_32_out, resultado[31]);
  and and_1 (and_1_out, not_1_out, not_2_out);
  and and_2 (and_2_out, and_29_out, not_10_out);
  and and_3 (and_3_out, and_30_out, not_18_out);
  and and_4 (and_4_out, and_31_out, not_26_out);
  and and_5 (and_5_out, and_1_out, not_3_out);
  and and_6 (and_6_out, and_2_out, not_11_out);
  and and_7 (and_7_out, and_3_out, not_19_out);
  and and_8 (and_8_out, and_4_out, not_27_out);
  and and_9 (and_9_out, and_5_out, not_4_out);
  and and_10 (and_10_out, and_9_out, not_5_out);
  and and_11 (and_11_out, and_6_out, not_12_out);
  and and_12 (and_12_out, and_7_out, not_20_out);
  and and_13 (and_13_out, and_8_out, not_28_out);
  and and_14 (and_14_out, and_11_out, not_13_out);
  and and_15 (and_15_out, and_12_out, not_21_out);
  and and_16 (and_16_out, and_13_out, not_29_out);
  and and_17 (and_17_out, and_10_out, not_6_out);
  and and_18 (and_18_out, and_14_out, not_14_out);
  and and_19 (and_19_out, and_15_out, not_22_out);
  and and_20 (and_20_out, and_16_out, not_30_out);
  and and_21 (and_21_out, and_17_out, not_7_out);
  and and_22 (and_22_out, and_18_out, not_15_out);
  and and_23 (and_23_out, and_19_out, not_23_out);
  and and_24 (and_24_out, and_20_out, not_31_out);
  and and_25 (and_25_out, and_21_out, not_8_out);
  and and_26 (and_26_out, and_22_out, not_16_out);
  and and_27 (and_27_out, and_23_out, not_24_out);
  and and_28 (tudo_zero, and_24_out, not_32_out);
  and and_29 (and_29_out, and_25_out, not_9_out);
  and and_30 (and_30_out, and_26_out, not_17_out);
  and and_31 (and_31_out, and_27_out, not_25_out);
endmodule
